# Fritzing sketch circuit (saved by Fritzing 0.8.6b)
breadboards: 1

parts:
  Raspberry_Pi_A1 = Raspberry Pi A
  R1 = Resistor [tolerance=±5% resistance=10k package=THT]
  S1 = Round Pushbutton  # not connected
  S2 = Round Pushbutton  # not connected
  S3 = Round Pushbutton  # not connected

nets:
  3V3: Raspberry_Pi_A1.3V3, Raspberry_Pi_A1.5V
  N1: Raspberry_Pi_A1.GND, R1.Pin_1
  N2: Raspberry_Pi_A1.GPIO_14, R1.Pin_0
